# Fritzing sketch BS2_moist_sensor (saved by Fritzing 0.9.3b)
breadboards: 1

parts:
  Parallax_BS2 = IC, DIP package, 24 pins [chip_label=IC]
  555_Timer_(Astable_Multivibrator) = IC, DIP package, 8 pins [chip_label=IC]
  C1 = Ceramic Capacitor [capacitance=0.1µF package="100 mil [THT, multilayer]"]
  R2 = Resistor [tolerance=±5% resistance=100 package=THT]
  Probes = mystery part, 2 pins [chip_label=?]
  U1 = Voltage Regulator - 5V [package="TO220 [THT]"]
  Power_plug1 = Power plug
  LED1 = LED - 5mm [color="Red (633nm)" package="5 mm [THT]"]
  R3 = Resistor [tolerance=±5% resistance=220 package=THT]
  Potentiometer = Rotary Potentiometer (Small) [maximum_resistance=10kΩ package=THT]
  C2 = Ceramic Capacitor [capacitance=10nF package="100 mil [THT, multilayer]"]
  R4 = Resistor [tolerance=±5% resistance=220 package=THT]

nets:
  N1: Parallax_BS2.pin4, Potentiometer.leg2, C2.1
  N2: Parallax_BS2.pin8, R3.Pin_1
  N3: Parallax_BS2.pin11, R4.Pin_0
  N4: Parallax_BS2.pin14, 555_Timer_(Astable_Multivibrator).pin4
  N5: Parallax_BS2.pin16, R2.Pin_0
  GND: Parallax_BS2.pin21, 555_Timer_(Astable_Multivibrator).pin1, C1.1, U1.GND, Power_plug1.GND, LED1.cathode
  N6: Parallax_BS2.pin23, 555_Timer_(Astable_Multivibrator).pin8
  N7: Parallax_BS2.pin24, U1.output_voltage
  N8: 555_Timer_(Astable_Multivibrator).pin2, 555_Timer_(Astable_Multivibrator).pin6, C1.0, Probes.pin2
  N9: 555_Timer_(Astable_Multivibrator).pin3, R2.Pin_1, Probes.pin1
  N10: U1.input_voltage, Power_plug1.VCC
  N11: LED1.anode, R3.Pin_0
  N12: Potentiometer.leg1, C2.0, R4.Pin_1
